# Fritzing sketch Esquematico_UNO-MATE_vFinal (saved by Fritzing 1.0.1rc)
breadboards: 1

parts:
  Mod1 = Raspberry Pi 4B
  Componente1 = Adafruit MAX98357A I2S 3W Class D Amplifier [part_number="Adafruit #3006"]
  M1 = DC Motor [voltage_(max)=6V voltage_(min)=3V]
  SPKR1 = Loudspeaker
  M2 = DC Motor [voltage_(max)=6V voltage_(min)=3V]
  6xAA_Battery1 = 6xAA Battery
  Componente3 = Arduino Nano (Rev3.0) (ICSP)
  L298N1 = L298N DC motor driver

nets:
  5V: Mod1.5V, Componente1.VIN
  N1: Mod1.GPIO18, Componente1.BCLK
  N2: Mod1.GPIO6, Mod1.GPIO13, Mod1.GPIO19, Componente1.LRCLK
  GND: Mod1.GND, Componente1.GND
  N3: Mod1.GPIO16, Mod1.GPIO20, Mod1.GPIO21, Componente1.DIN
  N4: Componente1.VO-, SPKR1.pin1
  N5: Componente1.VO+, SPKR1.pin2
  N6: M1.pin_1, L298N1.OUT2
  N7: M1.pin_2, L298N1.OUT1
  N8: M2.pin_1, L298N1.OUT4
  N9: M2.pin_2, L298N1.OUT3
  GND_2: 6xAA_Battery1.Pin_1, Componente3.GND, L298N1.GND
  N10: 6xAA_Battery1.Pin_2, L298N1.12V
  N11: Componente3.RESET, L298N1.5V#7
  N12: Componente3.D4, L298N1.IN4
  N13: Componente3.D5, L298N1.IN3
  N14: Componente3.D8, L298N1.IN2
  N15: Componente3.D9, L298N1.IN1
  N16: L298N1.5V#9, L298N1.ENA
  N17: L298N1.5V#10, L298N1.ENB

custom parts:
  Adafruit MAX98357A I2S 3W Class D Amplifier: Listen to this good news - we now have an all in one digital audio amp breakout board that works incredibly well with the Raspberry Pi! If you're looking for an easy and low cost way to get you digital sound files bumpin' then the MAX08357 I2S Amp Breakout is for you. It takes standard I2S digital audio input and, not only decodes it into analog, but also amplifies it directly into a speaker.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
  6xAA Battery: 6xAA battery
  L298N DC motor driver: 2x DC motor driver with 78M05 positive voltage regulator (7..35 V) L298N: max 46 V, 2 A Set 5 V Enable jumper to enable 5 V regultor (needed for the L298N) and +5 V output at screw terminal or supply external +5 V at screw terminal Set ENA and/or ENB to +5 V to enable motor permanently or supply ENA and/or ENB with PWM signal IN1 and IN2 set rotation directory for motor A (OUT1/OUT2) IN2 and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
